# Fritzing sketch Weather Station (saved by Fritzing 0.9.2b)
breadboards: 1

parts:
  Raspberry_Pi1 = Raspberry Pi B+
  DHT2 = DHT22 Humidity and Temperature Sensor
  GPS_Reciever = SUP500F [package=sup500f]
  R1 = Resistor [tolerance=±20% resistance=10k package=THT]
  Part1 = BMP180 Breakout (GY-68)
  YL-83_-_Detection_Board1 = YL-83 Rain Sensor - Detection Board
  YL-83_-_Control_Board1 = YL-83 Rain Sensor - Control Board
  Part2 = Arduino Uno (Rev3) - ICSP
  Part3 = Adafruit MiCS-5524 Gas Sensor [part_number="Adafruit #3199"]
  R2 = Photocell (LDR) [package=THT]
  R3 = Resistor [tolerance=±5% resistance=10k package="2512 [SMD]"]

nets:
  3V3: Raspberry_Pi1.3v3, DHT2.VDD, R1.Pin_0, Part1.VCC
  N1: Raspberry_Pi1.GPIO2, Part1.SDA
  N2: Raspberry_Pi1.GPIO3, Part1.SCL
  GND: Raspberry_Pi1.GPIO4, Raspberry_Pi1.GND, DHT2.DATA, DHT2.NULL, DHT2.GND, GPS_Reciever.GND, R1.Pin_1, Part1.GND
  N3: Raspberry_Pi1.GPIO18, Raspberry_Pi1.GPIO15, GPS_Reciever.TX-O
  N4: Raspberry_Pi1.GPIO14, GPS_Reciever.RX-I
  N5: YL-83_-_Detection_Board1.POS, YL-83_-_Control_Board1.POS
  N6: YL-83_-_Detection_Board1.NEG, YL-83_-_Control_Board1.NEG
  VCC: YL-83_-_Control_Board1.VCC, Part2.5V, Part3.5.0V, R3.Pin_1
  GND_2: YL-83_-_Control_Board1.GND, Part2.GND, Part3.GND, R2.pin_0
  N7: YL-83_-_Control_Board1.AO, Part2.A0
  N8: Part2.A1, R2.pin_1, R3.Pin_0
  N9: Part2.A2, Part3.AOUT

custom parts:
  BMP180 Breakout (GY-68): This is a simple breakout board for the BMP180, a high-precision, low-power barometric pressure sensor made by Bosch Sensortec. The range of measurement is from 300hPa to 1100hPa. The sensor can be supplied with voltage ranging from 1.8V to 3.6V. Operating temperature range is -40 to +85 °C. This particular breakout board (or perhaps the configuration) is produced by Shenzhen Keep Power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
  YL-83 Rain Sensor - Detection Board: The YL-83 is a rain sensor that has more resistance when dry and less resistance when wet. The module runs at 5V.
  YL-83 Rain Sensor - Control Board: The YL-83 is a rain sensor that has more resistance when dry and less resistance when wet. The module runs at 5V.
  Adafruit MiCS-5524 Gas Sensor: Give your next sensor project a nose for gasses with the Adafruit MiCS-5524 Gas Sensor Breakout. This breakout makes it easy to use this nice sensor from SGX Sensortech. The MiCS-5524 is a robust MEMS sensor for indoor carbon monoxide and natural gas leakage detection, it's suitable also for indoor air quality monitoring; breath checker and early fire detection. Please note: This sensor is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
